# Fritzing sketch circuit (saved by Fritzing 0.9.4)
circuit board: 3.25497cm x 3.33022cm

parts:
  Bauteil1 = Adafruit Micro USB Breakout [part_number="Adafruit #1833"]
  Bauteil2 = Adafruit TPL5110 Power Timer [part_number="Adafruit #3435"]
  MCU1 = Raspberry Pi Zero
  C2 = Ceramic Capacitor [capacitance=100nF package="200 mil [THT, multilayer]"]
  R1 = Resistor [tolerance=±5% resistance=10k package=THT]
  R2 = Resistor [tolerance=±5% resistance=100k package=THT]
  R3 = Resistor [tolerance=±5% resistance=180k package=THT]
  S2 = Toggle Switch [package=THT]
  DONE = Pad [width=4 height=4 connect=center]
  DLY = Pad [width=4 height=4 connect=center]
  DRV = Pad [width=4 height=4 connect=center]
  5V = Pad [width=4 height=4 connect=center]
  GND = Pad [width=4 height=4 connect=center]
  GND_2 = Pad [width=4 height=4 connect=center]
  U1_1 = 74LS74-Flipflops [part_number=74LS74 package="DIP (Dual Inline) [THT]"]
  U1 = 74LS74-Flipflops [part_number=74LS74 package="DIP (Dual Inline) [THT]"]
  Bauteil3 = 74LS74-Flipflops [part_number=74LS74 package="DIP (Dual Inline) [THT]"]
  U1_2 = 74LS74-Flipflops [part_number=74LS74 package="DIP (Dual Inline) [THT]"]
  GND2 = Pad [width=4 height=4 connect=center]
  PIN = Pad [width=4 height=4 connect=center]
  C3 = Electrolytic Capacitor [capacitance=0.47mF package="100 mil [THT, electrolytic]"]
  C4 = Electrolytic Capacitor [capacitance=0.47mF package="100 mil [THT, electrolytic]"]

nets:
  GND: Bauteil1.GND, Bauteil2.GND, MCU1.pin_6, MCU1.pin_39, C2.0, R2.Pin_0, R3.Pin_0, S2.L1, GND.pad, GND_2.pad, U1.connector6, Bauteil3.7, GND2.pad, C3.-, C4.-
  N1: Bauteil1.VBUS, Bauteil2.VDD, C3.+
  N2: Bauteil2.DELAY, R3.Pin_1, DLY.pad
  N3: Bauteil2.PWROUT, MCU1.pin_4, R1.Pin_1, DRV.pad, 5V.pad, U1_1.2, U1_1.4, U1.connector1, U1.connector3, U1.connector9, U1.connector13, Bauteil3.14, U1_2.10, C4.+
  N4: Bauteil2.DONE, S2.COM, DONE.pad
  N5: MCU1.pin_32, U1_1.3, U1_2.11
  N6: C2.1, R1.Pin_0, R2.Pin_1, U1_1.1, U1.connector0, U1.connector12, U1_2.13
  N7: S2.L2, U1.connector8, U1_2.9
  N8: U1_1.5, U1_2.12
  N9: U1.connector2, U1.connector10, PIN.pad
  N10: U1.connector4, U1.connector11

notes:
  rpi-timer v1.0

custom parts:
  Adafruit Micro USB Breakout: Simple but effective - this breakout board has a USB Micro-B connector, with all 5 pins broken out. Great for pairing with a microcontroller with USB support, or adding USB 5V power to a project. We use a micro-AB connector with through-hole shielding pads for an excellent strong connection - it won't rip off by accident! Comes with one fully assembled and tested micro B breakout PCB and a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
  Adafruit TPL5110 Power Timer: With some development boards, low power usage is an afterthought. Especially when price and usability is the main selling point. So what should you do when its time to turn around and make that project of yours run on a battery or solar? Sure you could try to hot-air that regulator off, or you could jerry-rig a relay. Or, use a 555? Ugh, the options aren't that great. The Adafruit TPL5110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
